# Fritzing sketch Diagram (saved by Fritzing 0.9.10b)
breadboards: 1

parts:
  Part1 = Arduino Mega 2560 (Rev3)
  Part2 = InvenSense MPU6050
  J1 = female pin header, 2 pins [form="♀ (female)"]
  J2 = female pin header, 2 pins [form="♀ (female)"]
  J3 = female pin header, 2 pins [form="♀ (female)"]
  J4 = female pin header, 2 pins [form="♀ (female)"]
  U2 = LCD-16X2 [package=lcd-16x2]
  R1 = Rotary Potentiometer (Small) [maximum_resistance=100kΩ knob_status=50% power=0.5W package=THT]

nets:
  N1: Part1.D21/SCL, Part2.SCL
  N2: Part1.D20/SDA, Part2.SDA
  N3: Part1.D17_PWM/RX2, J3.pin1
  N4: Part1.D15/RX3, J2.pin1
  N5: Part1.D14/TX3, J1.pin2
  N6: Part1.VIN, J1.pin1
  N7: Part1.D1_TX0, U2.RS
  N8: Part1.D2_PWM, U2.E
  N9: Part1.D4_PWM, U2.DB7
  N10: Part1.D5_PWM, U2.DB6
  N11: Part1.D6_PWM, U2.DB5
  N12: Part1.D7_PWM, U2.DB4
  5V: Part1.5V, Part2.VCC, J3.pin2, U2.VDD, U2.A, R1.leg1
  GND: Part1.GND, Part2.GND, J2.pin2, J4.pin1, U2.VSS, U2.R_W, U2.K, R1.leg2
  N13: U2.VO, R1.wiper

notes:
  HB_12V Out
  HB_TX
  HB_RX
  HB_GND
  FS_GND
  FS_IBUS
  FS_VIN
